// Digital circuit CPU.dig as structural Verilog
module CPU (
  input  clk,
  input  clk_2,
  input  [31:0] Interface
);

  wire button_1_out, button_2_out, Clk_t, CopyClk, counter_1_ovf, Ctrl_InterfaceOut, Ctrl_MemAdrIn,
       Ctrl_MemOut, Ctrl_MemRevOut, dipswitch_5_out, dipswitch_6_out, not_1_out, or_1_out;
  wire [3:0] multiplexer_3_out, multiplexer_3_out_2, multiplexer_3_out_3, multiplexer_3_out_4,
       multiplexer_3_out_5;
  wire [15:0] Boot_d, Boot_d_2;
  wire [23:0] counter_1_out, RAM_Address_q;
  wire [23:20] multiplexer_3_out_6;
  wire [31:0] Bus;

  not not_1 (not_1_out, or_1_out);
  Counter #(.Bits(24)) counter_1 (.en(not_1_out), .C(CopyClk), .clr(1'b0), .out(counter_1_out), .ovf(counter_1_ovf));
  DipSwitch dipswitch_1 (.out(Ctrl_MemOut));
  DipSwitch dipswitch_2 (.out(Ctrl_MemRevOut));
  DipSwitch dipswitch_3 (.out(Ctrl_MemAdrIn));
  DipSwitch dipswitch_4 (.out(Ctrl_InterfaceOut));
  Button button_1 (.out(button_1_out));
  Multiplexer multiplexer_1 (.sel(dipswitch_5_out), .in_0(button_1_out), .in_1(clk_2), .out(Clk_t));
  DipSwitch dipswitch_5 (.out(dipswitch_5_out));
  Button button_2 (.out(button_2_out));
  Multiplexer multiplexer_2 (.sel(dipswitch_6_out), .in_0(button_2_out), .in_1(clk), .out(CopyClk));
  DipSwitch dipswitch_6 (.out(dipswitch_6_out));
  or or_1 (or_1_out, or_1_out, counter_1_ovf);
  Multiplexer #(.Bits(24)) multiplexer_3 (
    .sel(not_1_out), .in_0(RAM_Address_q), .in_1(counter_1_out),
    .out({multiplexer_3_out_6, multiplexer_3_out_5, multiplexer_3_out_4, multiplexer_3_out_3, multiplexer_3_out_2, multiplexer_3_out}));
  ROM #(.bigEndian("true"), .AddrBits(24), .Bits(32)) Boot (
    .A({multiplexer_3_out_6, multiplexer_3_out_5, multiplexer_3_out_4, multiplexer_3_out_3, multiplexer_3_out_2, multiplexer_3_out}),
    .sel(not_1_out), .D({Boot_d_2, Boot_d}));
  RAMSinglePort #(.AddrBits(24), .Bits(32)) ramsingleport_1 (
    .A({multiplexer_3_out_6, multiplexer_3_out_5, multiplexer_3_out_4, multiplexer_3_out_3, multiplexer_3_out_2, multiplexer_3_out}),
    .str(not_1_out), .C(CopyClk), .ld(or_1_out), .D({Boot_d_2, Boot_d}));
  Seven_Seg_Hex seven_seg_hex_1 (.d(multiplexer_3_out_6), .dp(1'b0));
  Seven_Seg_Hex seven_seg_hex_2 (.d(multiplexer_3_out_5), .dp(1'b0));
  Seven_Seg_Hex seven_seg_hex_3 (.d(multiplexer_3_out_4), .dp(1'b0));
  Register #(.Bits(24)) RAM_Address (.D(Bus[23:0]), .C(Clk_t), .en(Ctrl_MemAdrIn), .Q(RAM_Address_q));
  Seven_Seg_Hex seven_seg_hex_4 (.d(multiplexer_3_out_3), .dp(1'b0));
  assign Bus = Ctrl_MemOut ? {Boot_d_2, Boot_d} : 32'bz;  // Driver driver_1
  assign Bus = Ctrl_MemRevOut ? {Boot_d, Boot_d_2} : 32'bz;  // Driver driver_2
  assign Bus = Ctrl_InterfaceOut ? Interface : 32'bz;  // Driver driver_3
  Seven_Seg_Hex seven_seg_hex_5 (.d(multiplexer_3_out_2), .dp(1'b0));
  Seven_Seg_Hex seven_seg_hex_6 (.d(multiplexer_3_out), .dp(1'b0));
  Seven_Seg_Hex seven_seg_hex_7 (.d(Boot_d_2[15:12]), .dp(1'b0));
  Seven_Seg_Hex seven_seg_hex_8 (.d(Bus[31:28]), .dp(1'b0));
  Seven_Seg_Hex seven_seg_hex_9 (.d(Boot_d_2[11:8]), .dp(1'b0));
  Seven_Seg_Hex seven_seg_hex_10 (.d(Bus[27:24]), .dp(1'b0));
  Seven_Seg_Hex seven_seg_hex_11 (.d(Boot_d_2[7:4]), .dp(1'b0));
  Seven_Seg_Hex seven_seg_hex_12 (.d(Bus[23:20]), .dp(1'b0));
  Seven_Seg_Hex seven_seg_hex_13 (.d(Boot_d_2[3:0]), .dp(1'b0));
  Seven_Seg_Hex seven_seg_hex_14 (.d(Bus[19:16]), .dp(1'b0));
  Seven_Seg_Hex seven_seg_hex_15 (.d(Boot_d[15:12]), .dp(1'b0));
  Seven_Seg_Hex seven_seg_hex_16 (.d(Bus[15:12]), .dp(1'b0));
  Seven_Seg_Hex seven_seg_hex_17 (.d(Boot_d[11:8]), .dp(1'b0));
  Seven_Seg_Hex seven_seg_hex_18 (.d(Bus[11:8]), .dp(1'b0));
  Seven_Seg_Hex seven_seg_hex_19 (.d(Boot_d[7:4]), .dp(1'b0));
  Seven_Seg_Hex seven_seg_hex_20 (.d(Bus[7:4]), .dp(1'b0));
  Seven_Seg_Hex seven_seg_hex_21 (.d(Boot_d[3:0]), .dp(1'b0));
  Seven_Seg_Hex seven_seg_hex_22 (.d(Bus[3:0]), .dp(1'b0));

  // Notes on the sheet:
  //   clk: Hz: 2147483647
  //   clk_2: Hz: 10
  //   Memory Address
  //   Boot loads boot.spy
  //   Memory Word
  //   Bus
endmodule
