// Digital circuit CPU.dig as structural Verilog
module CPU (
  input  clk,
  input  clk_2,
  input  [31:0] Interface,
  input  clk_3
);

  wire and_2_out, and_5_out, and_6_out, and_7_out, BootSeq_Active, BootSeq_p2, button_1_out, Clk_t,
       comparator_1_eq, Ctrl_Alloc, Ctrl_AllocOut, Ctrl_BusMux0, Ctrl_BusMux1, Ctrl_DeAlloc, Ctrl_ExecEn,
       Ctrl_ExecInst, Ctrl_Halt, Ctrl_InterfaceOut, Ctrl_LoadInst, Ctrl_MemAddrIn, Ctrl_MemDataIn,
       Ctrl_MemDataOut, Ctrl_PC_Out, Ctrl_PCIn, Ctrl_PCInc, Ctrl_SetFirstBlock, decoder_1_out_0,
       decoder_1_out_1, decoder_1_out_2, decoder_1_out_3, dipswitch_1_out, Exec_p2, Manual_p2, mmu_1_p9,
       mmu_1_p10, mmu_1_p11, multiplexer_4_out, multiplexer_5_out, multiplexer_6_out, nClk, nHalt, nHold,
       nor_1_out, not_2_out, not_3_out, not_5_out, not_6_out, not_7_out, or_2_out, or_3_out, or_4_out,
       or_5_out, or_6_out, or_7_out, or_8_out, or_9_out, or_10_out, or_11_out, or_12_out, or_13_out,
       rs_ff_as_2_q, rs_ff_as_3_q, ShadCp_Active, ShadCp_nActive, ShadCpClk, State_Set;
  wire [3:0] Step_out;
  wire [7:0] Instruction_q, multiplexer_7_out, Parameter_q, State, State_q, Validator_d;
  wire [17:12] driver_6_out;
  wire [31:0] Address, Boot_Sequencer_d, Bus_In, Bus_Out, Bytecode_Executor_d, MemAddrIn_out, MemoryAddr_q,
       mmu_1_p7, mmu_1_p8, multiplexer_3_out, Program_Counter_out, ShadCp_Addr;

  PullDown #(.Bits(32)) pulldown_1 (.out(Bus_In));
  and and_1 (ShadCpClk, clk, ShadCp_Active);
  not not_1 (ShadCp_Active, ShadCp_nActive);
  Counter #(.Bits(32)) counter_1 (.en(ShadCp_Active), .C(ShadCpClk), .clr(1'b0), .out(ShadCp_Addr));  // open: ovf
  // MMU mmu_1: pin names not known; wires that end beside it: Ctrl_Alloc, Ctrl_DeAlloc, Ctrl_AllocOut, Ctrl_SetFirstBlock, Clk_t, Bus_Out, mmu_1_p7, mmu_1_p8, mmu_1_p9, mmu_1_p10, mmu_1_p11
  or or_1 (ShadCp_nActive, ShadCp_nActive, comparator_1_eq);
  Comparator #(.Bits(32)) comparator_1 (.a(ShadCp_Addr), .b(32'h100000), .eq(comparator_1_eq));  // open: gt, lt
  Register #(.Bits(32)) MemoryAddr (.D(Bus_Out), .C(Clk_t), .en(Ctrl_MemAddrIn), .Q(MemoryAddr_q));
  Multiplexer #(.Selector_Bits(2), .Bits(32)) multiplexer_1 (
    .sel({Ctrl_BusMux1, Ctrl_BusMux0}), .in_0(Bus_In), .in_1({Bus_In[23:0], Bus_In[31:24]}),
    .in_2({Bus_In[15:0], Bus_In[31:24], Bus_In[15:8]}), .in_3({Bus_In[7:0], Bus_In[31:8]}), .out(Bus_Out));
  Decoder #(.Selector_Bits(2)) decoder_1 (
    .sel({Ctrl_BusMux1, Ctrl_BusMux0}), .out_0(decoder_1_out_0), .out_1(decoder_1_out_1),
    .out_2(decoder_1_out_2), .out_3(decoder_1_out_3));
  PullDown #(.Bits(32)) pulldown_2 (.out(Bus_Out));
  LED ABCD (.in(decoder_1_out_0));
  LED BCDA (.in(decoder_1_out_1));
  LED CDAB (.in(decoder_1_out_2));
  LED DABC (.in(decoder_1_out_3));
  Multiplexer #(.Bits(32)) multiplexer_2 (
    .sel(ShadCp_nActive), .in_0(ShadCp_Addr), .in_1(multiplexer_3_out), .out(Address));
  Multiplexer #(.Bits(32)) multiplexer_3 (
    .sel(mmu_1_p11), .in_0(mmu_1_p7), .in_1(MemoryAddr_q), .out(multiplexer_3_out));
  or or_2 (or_2_out, ShadCpClk, Clk_t);
  Multiplexer multiplexer_4 (.sel(mmu_1_p11), .in_0(mmu_1_p9), .in_1(Ctrl_MemDataIn), .out(multiplexer_4_out));
  Multiplexer multiplexer_5 (.sel(mmu_1_p11), .in_0(mmu_1_p10), .in_1(Ctrl_MemDataOut), .out(multiplexer_5_out));
  or or_3 (or_3_out, ShadCp_Active, multiplexer_4_out);
  LED led_1 (.in(and_2_out));
  and and_2 (and_2_out, clk_3, or_5_out);
  Button button_1 (.out(button_1_out));
  Multiplexer multiplexer_6 (.sel(dipswitch_1_out), .in_0(button_1_out), .in_1(clk_2), .out(multiplexer_6_out));
  DipSwitch dipswitch_1 (.out(dipswitch_1_out));
  PullUp pullup_1 (.out(nHalt));
  not not_2 (not_2_out, nHalt);
  // ROM rom_1: pin names not known; wires that end beside it: Address, ShadCp_Active, mmu_1_p8
  and and_3 (nHold, ShadCp_nActive, mmu_1_p11);
  or or_4 (or_4_out, Ctrl_MemDataOut, ShadCp_Active);
  RAM ram_1 (.Addr(Address), .Str(or_3_out), .Clk(or_2_out), .Ld(multiplexer_5_out), .D(mmu_1_p8));
  or or_5 (or_5_out, not_2_out, or_5_out);
  and and_4 (Clk_t, multiplexer_6_out, not_3_out);
  not not_3 (not_3_out, or_5_out);
  assign nHalt = Ctrl_Halt ? 1'b0 : 1'bz;  // Driver driver_1
  assign Bus_In = or_4_out ? mmu_1_p8 : 32'bz;  // Driver driver_2
  assign mmu_1_p8 = Ctrl_MemDataIn ? Bus_Out : 32'bz;  // Driver driver_3
  not not_4 (nClk, Clk_t);
  and and_5 (and_5_out, State_Set, not_5_out);
  Multiplexer #(.Bits(8)) multiplexer_7 (.sel(State_Set), .in_0(Instruction_q), .in_1(State), .out(multiplexer_7_out));
  ROM #(.bigEndian("true"), .AddrBits(8), .Bits(8)) Validator (.A(Instruction_q), .sel(1'b1), .D(Validator_d));
  CounterPreset #(.Bits(32), .isProgramCounter("true")) Program_Counter (
    .en(Ctrl_PCInc), .C(Clk_t), .dir(1'b0), .in(Bus_Out), .ld(Ctrl_PCIn), .clr(1'b0),
    .out(Program_Counter_out));  // open: ovf
  or or_6 (or_6_out, and_5_out, or_7_out);
  or or_7 (or_7_out, Ctrl_ExecEn, Ctrl_ExecInst);
  not not_5 (not_5_out, BootSeq_Active);
  or or_8 (or_8_out, State_Set, Ctrl_ExecInst);
  not not_6 (not_6_out, Validator_d[0]);
  Register #(.Bits(8)) Instruction (.D(Bus_Out[31:24]), .C(Clk_t), .en(Ctrl_LoadInst), .Q(Instruction_q));
  Register #(.Bits(8)) Parameter (.D(Bus_Out[23:16]), .C(Clk_t), .en(Ctrl_LoadInst), .Q(Parameter_q));
  // Probe on Program_Counter_out
  assign Bus_In = Ctrl_PC_Out ? Program_Counter_out : 32'bz;  // Driver driver_4
  Counter #(.Bits(4)) Step (.en(nHold), .C(Clk_t), .clr(or_6_out), .out(Step_out));  // open: ovf
  Register #(.Bits(8)) u_State (.D(multiplexer_7_out), .C(Clk_t), .en(or_8_out), .Q(State_q));
  LED led_2 (.in(not_6_out));
  assign nHalt = not_6_out ? 1'b0 : 1'bz;  // Driver driver_5
  Seven_Seg_Hex seven_seg_hex_1 (.d(State_q[7:4]), .dp(1'b0));
  Seven_Seg_Hex seven_seg_hex_2 (.d(Instruction_q[7:4]), .dp(1'b0));
  Seven_Seg_Hex seven_seg_hex_3 (.d(Address[31:28]), .dp(1'b0));
  ROM #(.bigEndian("true"), .AddrBits(4), .Bits(32)) Boot_Sequencer (.A(Step_out), .sel(1'b1), .D(Boot_Sequencer_d));
  ROM #(.bigEndian("true"), .AddrBits(16), .Bits(32)) Bytecode_Executor (
    .A({State_q, Step_out, 4'b0001}), .sel(1'b1), .D(Bytecode_Executor_d));
  Seven_Seg_Hex seven_seg_hex_4 (.d(State_q[3:0]), .dp(1'b0));
  Seven_Seg_Hex seven_seg_hex_5 (.d(Instruction_q[3:0]), .dp(1'b0));
  Seven_Seg_Hex seven_seg_hex_6 (.d(Address[27:24]), .dp(1'b0));
  assign {State, State_Set, Ctrl_Halt, Ctrl_ExecEn, Ctrl_InterfaceOut, Ctrl_BusMux1, Ctrl_BusMux0, driver_6_out, Ctrl_PC_Out, Ctrl_PCIn, Ctrl_PCInc, Ctrl_ExecInst, Ctrl_LoadInst, Ctrl_AllocOut, Ctrl_SetFirstBlock, Ctrl_DeAlloc, Ctrl_Alloc, Ctrl_MemDataOut, Ctrl_MemDataIn, Ctrl_MemAddrIn} = BootSeq_Active ? Boot_Sequencer_d : 32'bz;  // Driver driver_6
  assign {State, State_Set, Ctrl_Halt, Ctrl_ExecEn, Ctrl_InterfaceOut, Ctrl_BusMux1, Ctrl_BusMux0, driver_6_out, Ctrl_PC_Out, Ctrl_PCIn, Ctrl_PCInc, Ctrl_ExecInst, Ctrl_LoadInst, Ctrl_AllocOut, Ctrl_SetFirstBlock, Ctrl_DeAlloc, Ctrl_Alloc, Ctrl_MemDataOut, Ctrl_MemDataIn, Ctrl_MemAddrIn} = rs_ff_as_2_q ? Bytecode_Executor_d : 32'bz;  // Driver driver_7
  PullDown #(.Bits(32)) pulldown_3 (.out({State, State_Set, Ctrl_Halt, Ctrl_ExecEn, Ctrl_InterfaceOut, Ctrl_BusMux1, Ctrl_BusMux0, driver_6_out, Ctrl_PC_Out, Ctrl_PCIn, Ctrl_PCInc, Ctrl_ExecInst, Ctrl_LoadInst, Ctrl_AllocOut, Ctrl_SetFirstBlock, Ctrl_DeAlloc, Ctrl_Alloc, Ctrl_MemDataOut, Ctrl_MemDataIn, Ctrl_MemAddrIn}));
  Seven_Seg_Hex seven_seg_hex_7 (.d(Address[23:20]), .dp(1'b0));
  Seven_Seg_Hex seven_seg_hex_8 (.d(Parameter_q[7:4]), .dp(1'b0));
  Seven_Seg_Hex seven_seg_hex_9 (.d(Address[19:16]), .dp(1'b0));
  nor nor_1 (nor_1_out, BootSeq_Active, rs_ff_as_2_q, rs_ff_as_3_q);
  not not_7 (not_7_out, rs_ff_as_2_q);
  Seven_Seg_Hex seven_seg_hex_10 (.d(Parameter_q[3:0]), .dp(1'b0));
  Seven_Seg_Hex seven_seg_hex_11 (.d(Address[15:12]), .dp(1'b0));
  RS_FF_AS rs_ff_as_1 (.S(or_12_out), .R(or_9_out), .Q(BootSeq_Active));  // open: nQ
  RS_FF_AS rs_ff_as_2 (.S(or_13_out), .R(or_10_out), .Q(rs_ff_as_2_q));  // open: nQ
  RS_FF_AS rs_ff_as_3 (.S(Manual_p2), .R(or_11_out), .Q(rs_ff_as_3_q));  // open: nQ
  Seven_Seg_Hex seven_seg_hex_12 (.d(Address[11:8]), .dp(1'b0));
  or or_9 (or_9_out, Manual_p2, or_13_out);
  or or_10 (or_10_out, Manual_p2, or_12_out);
  or or_11 (or_11_out, or_13_out, or_12_out);
  and and_6 (and_6_out, Ctrl_ExecEn, not_7_out);
  Seven_Seg_Hex seven_seg_hex_13 (.d(Address[7:4]), .dp(1'b0));
  and and_7 (and_7_out, ShadCp_nActive, nor_1_out);
  Seven_Seg_Hex seven_seg_hex_14 (.d(Address[3:0]), .dp(1'b0));
  or or_12 (or_12_out, and_7_out, BootSeq_p2);
  or or_13 (or_13_out, and_6_out, Exec_p2);
  // ButtonLED BootSeq: pin names not known; wires that end beside it: BootSeq_Active, BootSeq_p2
  // ButtonLED Exec: pin names not known; wires that end beside it: rs_ff_as_2_q, Exec_p2
  // ButtonLED Manual: pin names not known; wires that end beside it: rs_ff_as_3_q, Manual_p2
  Seven_Seg_Hex seven_seg_hex_15 (.d(Bus_Out[31:28]), .dp(1'b0));
  Seven_Seg_Hex seven_seg_hex_16 (.d(Bus_Out[27:24]), .dp(1'b0));
  Seven_Seg_Hex seven_seg_hex_17 (.d(Bus_Out[23:20]), .dp(1'b0));
  DipSwitch MemAddrIn (.out(MemAddrIn_out[0]));
  DipSwitch MemDataIn (.out(MemAddrIn_out[1]));
  DipSwitch MemDataOut (.out(MemAddrIn_out[2]));
  DipSwitch Alloc (.out(MemAddrIn_out[3]));
  DipSwitch Dealloc (.out(MemAddrIn_out[4]));
  DipSwitch SetFirstBlock (.out(MemAddrIn_out[5]));
  DipSwitch AllocOut (.out(MemAddrIn_out[6]));
  DipSwitch LoadInstr (.out(MemAddrIn_out[7]));
  DipSwitch ExecInstr (.out(MemAddrIn_out[8]));
  DipSwitch PCInc (.out(MemAddrIn_out[9]));
  DipSwitch PCIn (.out(MemAddrIn_out[10]));
  DipSwitch PCOut (.out(MemAddrIn_out[11]));
  DipSwitch dipswitch_2 (.out(MemAddrIn_out[12]));
  DipSwitch dipswitch_3 (.out(MemAddrIn_out[13]));
  DipSwitch dipswitch_4 (.out(MemAddrIn_out[14]));
  DipSwitch dipswitch_5 (.out(MemAddrIn_out[15]));
  DipSwitch dipswitch_6 (.out(MemAddrIn_out[16]));
  DipSwitch dipswitch_7 (.out(MemAddrIn_out[17]));
  DipSwitch BusMux0 (.out(MemAddrIn_out[18]));
  DipSwitch BusMux1 (.out(MemAddrIn_out[19]));
  DipSwitch InterfaceOut (.out(MemAddrIn_out[20]));
  DipSwitch ExecEn (.out(MemAddrIn_out[21]));
  DipSwitch Halt (.out(MemAddrIn_out[22]));
  DipSwitch u_State_Set (.out(MemAddrIn_out[23]));
  DipSwitch State_0 (.out(MemAddrIn_out[24]));
  DipSwitch State_1 (.out(MemAddrIn_out[25]));
  DipSwitch State_2 (.out(MemAddrIn_out[26]));
  DipSwitch State_3 (.out(MemAddrIn_out[27]));
  DipSwitch State_4 (.out(MemAddrIn_out[28]));
  DipSwitch State_5 (.out(MemAddrIn_out[29]));
  DipSwitch State_6 (.out(MemAddrIn_out[30]));
  DipSwitch State_7 (.out(MemAddrIn_out[31]));
  Seven_Seg_Hex seven_seg_hex_18 (.d(Bus_Out[19:16]), .dp(1'b0));
  assign {State, State_Set, Ctrl_Halt, Ctrl_ExecEn, Ctrl_InterfaceOut, Ctrl_BusMux1, Ctrl_BusMux0, driver_6_out, Ctrl_PC_Out, Ctrl_PCIn, Ctrl_PCInc, Ctrl_ExecInst, Ctrl_LoadInst, Ctrl_AllocOut, Ctrl_SetFirstBlock, Ctrl_DeAlloc, Ctrl_Alloc, Ctrl_MemDataOut, Ctrl_MemDataIn, Ctrl_MemAddrIn} = rs_ff_as_3_q ? MemAddrIn_out : 32'bz;  // Driver driver_8
  Seven_Seg_Hex seven_seg_hex_19 (.d(Bus_Out[15:12]), .dp(1'b0));
  Seven_Seg_Hex seven_seg_hex_20 (.d(Bus_Out[11:8]), .dp(1'b0));
  Seven_Seg_Hex seven_seg_hex_21 (.d(Bus_Out[7:4]), .dp(1'b0));
  Seven_Seg_Hex seven_seg_hex_22 (.d(Bus_Out[3:0]), .dp(1'b0));
  assign Bus_In = Ctrl_InterfaceOut ? Interface : 32'bz;  // Driver driver_9

  // Notes on the sheet:
  //   clk: Hz: 2147483647
  //   clk_2: Hz: 500000
  //   clk_3: Hz: 4
  //   Bus Muxer
  //   Memory
  //   ABCD
  //   Clock
  //   Control
  //   Validator loads validInstructions.bin
  //   State
  //   Instruction
  //   Memory Address
  //   Boot_Sequencer loads ucodeBootSeq.bin
  //   Bytecode_Executor loads ucodeByteCodeExec.bin
  //   Parameter
  //   Override Control
  //   Bus
endmodule
