// Digital circuit RAM.dig as structural Verilog
module RAM (
  input  [31:0] Addr,
  input  Str,
  input  Clk,
  input  Ld,
  output [31:0] D
);

  RAMSinglePort ramsingleport_1 (.A(Addr[1:0]), .str(Str), .C(Clk), .ld(Ld), .D(D[0]));
  // Pins of 1 and 32 bits meet at D
  // Pins of 2 and 24 bits meet at Addr[23:0]
endmodule
