// Digital circuit ROM.dig as structural Verilog
module ROM (
  input  [31:0] Addr,
  input  Sel,
  output [31:0] D
);

  ROM #(.bigEndian("true"), .AddrBits(24), .Bits(32)) Boot_ROM (.A(Addr[23:0]), .sel(Sel), .D(D));
  // Pins of 1 and 32 bits meet at D
  // Pins of 1 and 32 bits meet at Addr

  // Notes on the sheet:
  //   Boot_ROM loads boot.spy
endmodule
